// Logisim project Datapath.circ as structural Verilog: 11 circuits, main circuit main
module main (
  input  cin,
  input  Write_Enable,
  input  Reg_dis,
  input  ALU_src,
  input  RAM_to_reg,
  input  [2:0] ALU_opcode,
  input  Load_enable,
  input  Store_Enable,
  output [9:0] Result,
  output [3:0] OP,
  output [1:0] rs,
  output [1:0] rt,
  output [1:0] rd_imm,
  output [9:0] Data_1,
  output [9:0] Data_2
);

  wire clock_1_out;
  wire [1:0] multiplexer_1_out;
  wire [9:0] adder_1_out, bit_extender_1_out, multiplexer_2_out, multiplexer_3_out, ram_1_dout, register_1_q;

  Register #(.width(10)) register_1 (.D(adder_1_out), .Q(register_1_q), .clk(clock_1_out));  // open: en, clr
  ROM #(.addrWidth(10), .dataWidth(10)) rom_1 (.addr(register_1_q), .data({OP, rs, rt, rd_imm}));
  Adder #(.width(10)) adder_1 (.a(register_1_q), .b(10'h2), .out(adder_1_out));  // open: cin, cout
  Clock clock_1 (.out(clock_1_out));
  Multiplexer #(.width(2)) multiplexer_1 (.in0(rd_imm), .in1(rt), .out(multiplexer_1_out), .sel(Reg_dis));
  assign bit_extender_1_out = {{8{rt[1]}}, rt};  // Bit_Extender bit_extender_1
  register_file register_file_1 (
    .out_7(Data_1), .out_8(Data_2), .Write_Enable(Write_Enable), .Clock(clock_1_out),
    .in_1(multiplexer_3_out), .Rd(multiplexer_1_out), .rs(rs), .rt(rt));
  ten_bitALU ten_bitalu_1 (
    .out_6(Result), .in_5(multiplexer_2_out), .in_1(Data_1), .cin(cin), .ALU_opcode(ALU_opcode),
    .B_invert(cin));  // open: cout, overflow, zero_signal
  Multiplexer #(.width(10)) multiplexer_2 (
    .in0(Data_2), .in1(bit_extender_1_out), .out(multiplexer_2_out), .sel(ALU_src));
  RAM #(.addrWidth(10), .asyncread("true"), .dataWidth(10)) ram_1 (
    .addr(Result), .we(Store_Enable), .oe(Load_enable), .clk(clock_1_out), .din(Data_2), .dout(ram_1_dout));
  Multiplexer #(.width(10)) multiplexer_3 (.in0(Result), .in1(ram_1_dout), .out(multiplexer_3_out), .sel(RAM_to_reg));

  // Notes on the sheet:
  //   PC
  //   contents of rom_1 (hex, n*v repeats v):
  //   1ad 1ad 1ad 2ad
  //   Clock
endmodule

module one_bitALU (
  input  cin,
  input  Input_A,
  input  Input_B,
  input  B_invert,
  input  [2:0] in_5,
  output cout,
  output Result
);

  wire adder_1_out, and_1_out, multiplexer_1_out, not_1_out, or_1_out;

  not not_1 (not_1_out, Input_B);
  Multiplexer multiplexer_1 (.in0(Input_B), .in1(not_1_out), .out(multiplexer_1_out), .sel(B_invert));
  Adder #(.width(1)) adder_1 (.a(Input_A), .b(multiplexer_1_out), .out(adder_1_out), .cin(cin), .cout(cout));
  and and_1 (and_1_out, Input_A, multiplexer_1_out);
  or or_1 (or_1_out, Input_A, multiplexer_1_out);
  Multiplexer #(.select(3)) multiplexer_2 (
    .in0(adder_1_out), .in1(and_1_out), .in2(or_1_out), .out(Result), .sel(in_5));  // open: in3, in4, in5, in6, in7

  // Notes on the sheet:
  //   ALU opcode
endmodule

module ten_bitALU (
  input  [9:0] in_1,
  input  cin,
  input  B_invert,
  input  [2:0] ALU_opcode,
  input  [9:0] in_5,
  output [9:0] out_6,
  output zero_signal,
  output overflow,
  output cout
);

  wire one_bitalu_1_cout, one_bitalu_2_cout, one_bitalu_3_cout, one_bitalu_4_cout, one_bitalu_5_cout,
       one_bitalu_6_cout, one_bitalu_7_cout, one_bitalu_8_cout, one_bitalu_9_cout;

  one_bitALU one_bitalu_1 (
    .cout(one_bitalu_1_cout), .Result(out_6[0]), .B_invert(B_invert), .Input_A(in_1[0]), .cin(cin),
    .Input_B(in_5[0]), .in_5(ALU_opcode));
  one_bitALU one_bitalu_2 (
    .cout(one_bitalu_2_cout), .Result(out_6[1]), .B_invert(B_invert), .Input_A(in_1[1]),
    .cin(one_bitalu_1_cout), .Input_B(in_5[1]), .in_5(ALU_opcode));
  one_bitALU one_bitalu_3 (
    .cout(one_bitalu_3_cout), .Result(out_6[2]), .B_invert(B_invert), .Input_A(in_1[2]),
    .cin(one_bitalu_2_cout), .Input_B(in_5[2]), .in_5(ALU_opcode));
  one_bitALU one_bitalu_4 (
    .cout(one_bitalu_4_cout), .Result(out_6[3]), .B_invert(B_invert), .Input_A(in_1[3]),
    .cin(one_bitalu_3_cout), .Input_B(in_5[3]), .in_5(ALU_opcode));
  one_bitALU one_bitalu_5 (
    .cout(one_bitalu_5_cout), .Result(out_6[4]), .B_invert(B_invert), .Input_A(in_1[4]),
    .cin(one_bitalu_4_cout), .Input_B(in_5[4]), .in_5(ALU_opcode));
  one_bitALU one_bitalu_6 (
    .cout(one_bitalu_6_cout), .Result(out_6[5]), .B_invert(B_invert), .Input_A(in_1[5]),
    .cin(one_bitalu_5_cout), .Input_B(in_5[5]), .in_5(ALU_opcode));
  one_bitALU one_bitalu_7 (
    .cout(one_bitalu_7_cout), .Result(out_6[6]), .B_invert(B_invert), .Input_A(in_1[6]),
    .cin(one_bitalu_6_cout), .Input_B(in_5[6]), .in_5(ALU_opcode));
  one_bitALU one_bitalu_8 (
    .cout(one_bitalu_8_cout), .Result(out_6[7]), .B_invert(B_invert), .Input_A(in_1[7]),
    .cin(one_bitalu_7_cout), .Input_B(in_5[7]), .in_5(ALU_opcode));
  one_bitALU one_bitalu_9 (
    .cout(one_bitalu_9_cout), .Result(out_6[8]), .B_invert(B_invert), .Input_A(in_1[8]),
    .cin(one_bitalu_8_cout), .Input_B(in_5[8]), .in_5(ALU_opcode));
  one_bitALU one_bitalu_10 (
    .cout(cout), .Result(out_6[9]), .B_invert(B_invert), .Input_A(in_1[9]), .cin(one_bitalu_9_cout),
    .Input_B(in_5[9]), .in_5(ALU_opcode));
  xor xor_1 (overflow, one_bitalu_9_cout, cout);
  nor nor_1 (zero_signal, out_6[0], out_6[1], out_6[2], out_6[3], out_6[4], out_6[5], out_6[6], out_6[7], out_6[8], out_6[9]);

  // Notes on the sheet:
  //   A
  //   B
  //   Result
endmodule

module register_file (
  input  [9:0] in_1,
  input  [1:0] Rd,
  input  [1:0] rs,
  input  [1:0] rt,
  input  Write_Enable,
  input  Clock,
  output [9:0] out_7,
  output [9:0] out_8
);

  wire and_1_out, and_2_out, and_3_out, and_4_out, decoder_1_out0, decoder_1_out1, decoder_1_out2,
       decoder_1_out3;
  wire [9:0] register_1_q, register_2_q, register_3_q, register_4_q;

  Decoder #(.enable("false"), .select(2)) decoder_1 (
    .out0(decoder_1_out0), .out1(decoder_1_out1), .out2(decoder_1_out2), .out3(decoder_1_out3), .sel(Rd));
  and and_1 (and_1_out, decoder_1_out0, Write_Enable);
  and and_2 (and_2_out, decoder_1_out1, Write_Enable);
  and and_3 (and_3_out, decoder_1_out2, Write_Enable);
  and and_4 (and_4_out, decoder_1_out3, Write_Enable);
  Register #(.width(10)) register_1 (.D(in_1), .en(and_1_out), .Q(register_1_q), .clk(Clock));  // open: clr
  Register #(.width(10)) register_2 (.D(in_1), .en(and_2_out), .Q(register_2_q), .clk(Clock));  // open: clr
  Register #(.width(10)) register_3 (.D(in_1), .en(and_3_out), .Q(register_3_q), .clk(Clock));  // open: clr
  Register #(.width(10)) register_4 (.D(in_1), .en(and_4_out), .Q(register_4_q), .clk(Clock));  // open: clr
  Multiplexer #(.select(2), .width(10)) multiplexer_1 (
    .in0(register_1_q), .in1(register_2_q), .in2(register_3_q), .in3(register_4_q), .out(out_7), .sel(rs));
  Multiplexer #(.select(2), .width(10)) multiplexer_2 (
    .in0(register_1_q), .in1(register_2_q), .in2(register_3_q), .in3(register_4_q), .out(out_8), .sel(rt));

  // Notes on the sheet:
  //   Write data
  //   s0
  //   s1
  //   s2
  //   s3
  //   Data 1
  //   Data 2
endmodule

module with_control (
  input  [9:0] in_1,
  output [9:0] Data_1,
  output [9:0] Data_2,
  output [9:0] Result,
  output [3:0] OP,
  output [1:0] rs,
  output [1:0] rt,
  output [1:0] rd_imm_offset
);

  wire and_1_out, clock_1_out, imp_1_alu_src, imp_1_beq, imp_1_j, imp_1_load, imp_1_ram_to_reg,
       imp_1_reg_dis, imp_1_store, imp_1_sub, imp_1_write_enable, ten_bitalu_1_zero_signal;
  wire [1:0] multiplexer_3_out;
  wire [2:0] imp_1_alu_op;
  wire [5:0] adder_1_out_2;
  wire [9:0] adder_2_out, bit_extender_1_out, multiplexer_2_out, multiplexer_4_out, multiplexer_5_out,
       ram_1_dout, register_1_q, shifter_1_out;
  wire [9:6] adder_1_out;

  and and_1 (and_1_out, ten_bitalu_1_zero_signal, imp_1_beq);
  Multiplexer #(.width(10)) multiplexer_1 (
    .in0({adder_1_out, adder_1_out_2}), .in1(adder_2_out), .sel(and_1_out));  // open: out
  Multiplexer #(.width(10)) multiplexer_2 (
    .in0({adder_1_out, adder_1_out_2}), .in1({adder_1_out, rs, rt, rd_imm_offset}), .out(multiplexer_2_out),
    .sel(imp_1_j));
  ROM #(.addrWidth(10), .dataWidth(10)) rom_1 (.addr(register_1_q), .data({OP, rs, rt, rd_imm_offset}));
  Register #(.width(10)) register_1 (.D(multiplexer_2_out), .Q(register_1_q), .clk(clock_1_out));  // open: en, clr
  Clock clock_1 (.out(clock_1_out));
  imp imp_1 (
    .Reg_Dis(imp_1_reg_dis), .ALU_op(imp_1_alu_op), .ALU_src(imp_1_alu_src), .Load(imp_1_load),
    .Store(imp_1_store), .J(imp_1_j), .Beq(imp_1_beq), .RAM_to_reg(imp_1_ram_to_reg), .Sub(imp_1_sub),
    .write_enable(imp_1_write_enable), .opcode(OP));
  Adder #(.width(10)) adder_1 (.a(register_1_q), .b(10'h2), .out({adder_1_out, adder_1_out_2}));  // open: cin, cout
  assign bit_extender_1_out = {{8{rd_imm_offset[1]}}, rd_imm_offset};  // Bit_Extender bit_extender_1
  Multiplexer #(.width(2)) multiplexer_3 (.in0(rd_imm_offset), .in1(rt), .out(multiplexer_3_out), .sel(imp_1_reg_dis));
  register_file register_file_1 (
    .out_7(Data_1), .out_8(Data_2), .Write_Enable(imp_1_write_enable), .Clock(clock_1_out),
    .in_1(multiplexer_5_out), .Rd(multiplexer_3_out), .rs(rs), .rt(rt));
  Adder #(.width(10)) adder_2 (
    .a({adder_1_out, adder_1_out_2}), .b(shifter_1_out), .out(adder_2_out));  // open: cin, cout
  Shifter #(.width(10)) shifter_1 (.in(bit_extender_1_out), .\dist (in_1[3:0]), .out(shifter_1_out));
  Multiplexer #(.width(10)) multiplexer_4 (
    .in0(Data_2), .in1(bit_extender_1_out), .out(multiplexer_4_out), .sel(imp_1_alu_src));
  ten_bitALU ten_bitalu_1 (
    .out_6(Result), .zero_signal(ten_bitalu_1_zero_signal), .in_5(multiplexer_4_out), .in_1(Data_1),
    .cin(imp_1_sub), .ALU_opcode(imp_1_alu_op), .B_invert(imp_1_sub));  // open: cout, overflow
  RAM #(.addrWidth(10), .asyncread("true"), .dataWidth(10)) ram_1 (
    .addr(Result), .we(imp_1_store), .oe(imp_1_load), .clk(clock_1_out), .din(Data_2), .dout(ram_1_dout));
  Multiplexer #(.width(10)) multiplexer_5 (
    .in0(Result), .in1(ram_1_dout), .out(multiplexer_5_out), .sel(imp_1_ram_to_reg));

  // Notes on the sheet:
  //   Clock
  //   contents of rom_1 (hex, n*v repeats v):
  //   126 142 126 0 142 0 141 0 2ad 0 2ad 0 2ad 0 2ad 0 26d
  //   6 bit
  //   offset
endmodule

module control_Unit (
  input  [3:0] Opcode,
  output Write_Enable,
  output Reg_Dis,
  output [2:0] ALU_op,
  output ALU_src,
  output RAM_to_reg,
  output Load_Enable,
  output Store_Enable,
  output J,
  output Beq,
  output Sub
);

  wire and_1_out, and_2_out, and_3_out, and_4_out, and_8_out, and_9_out, and_15_out, and_16_out, and_17_out,
       not_1_out, not_2_out, not_3_out, not_4_out;

  not not_1 (not_1_out, Opcode[3]);
  not not_2 (not_2_out, Opcode[2]);
  not not_3 (not_3_out, Opcode[1]);
  not not_4 (not_4_out, Opcode[0]);
  and and_1 (and_1_out, not_2_out, not_3_out, not_4_out);
  and and_2 (and_2_out, not_1_out, Opcode[2], Opcode[1]);
  and and_3 (and_3_out, Opcode[3], not_2_out, not_3_out);
  and and_4 (and_4_out, Opcode[3], not_2_out, not_4_out);
  and and_5 (Reg_Dis, not_2_out, not_3_out, not_4_out);
  and and_6 (ALU_op[1], Opcode[3], not_2_out, Opcode[1], not_4_out);
  and and_7 (ALU_op[0], Opcode[3], not_2_out, not_3_out, Opcode[0]);
  and and_8 (and_8_out, not_1_out, not_3_out);
  and and_9 (and_9_out, not_2_out, not_3_out, not_4_out);
  and and_10 (RAM_to_reg, not_1_out, not_2_out, not_3_out, not_4_out);
  and and_11 (Load_Enable, not_1_out, not_2_out, not_3_out, not_4_out);
  and and_12 (Store_Enable, not_1_out, not_2_out, not_3_out, Opcode[0]);
  and and_13 (J, not_1_out, Opcode[2], not_3_out, Opcode[0]);
  and and_14 (Beq, not_1_out, Opcode[2], not_3_out, not_4_out);
  and and_15 (and_15_out, not_1_out, Opcode[2], not_3_out, not_4_out);
  and and_16 (and_16_out, not_1_out, Opcode[2], Opcode[1], Opcode[0]);
  and and_17 (and_17_out, Opcode[3], not_2_out, not_3_out, not_4_out);
  or or_1 (Write_Enable, and_1_out, and_2_out, and_3_out, and_4_out);
  or or_2 (ALU_src, and_8_out, and_9_out);
  or or_3 (Sub, and_15_out, and_16_out, and_17_out);

  assign ALU_op[2] = 1'b0;
endmodule

module imp (
  input  [3:0] opcode,
  output write_enable,
  output Reg_Dis,
  output [2:0] ALU_op,
  output ALU_src,
  output Load,
  output Store,
  output J,
  output Beq,
  output RAM_to_reg,
  output Sub
);

  wire and_1_out, and_2_out, and_3_out, and_4_out, and_8_out, and_9_out, and_15_out, and_16_out, and_17_out,
       not_1_out, not_2_out, not_3_out, not_4_out;

  not not_1 (not_1_out, opcode[3]);
  not not_2 (not_2_out, opcode[2]);
  not not_3 (not_3_out, opcode[1]);
  not not_4 (not_4_out, opcode[0]);
  and and_1 (and_1_out, not_2_out, not_3_out, not_4_out);
  and and_2 (and_2_out, not_1_out, opcode[2], opcode[1]);
  and and_3 (and_3_out, opcode[3], not_2_out, not_3_out);
  and and_4 (and_4_out, opcode[3], not_2_out, not_4_out);
  and and_5 (Reg_Dis, not_2_out, not_3_out, not_4_out);
  and and_6 (ALU_op[1], opcode[3], not_2_out, opcode[1], not_4_out);
  and and_7 (ALU_op[0], opcode[3], not_2_out, not_3_out, opcode[0]);
  and and_8 (and_8_out, not_1_out, not_3_out);
  and and_9 (and_9_out, not_2_out, not_3_out, not_4_out);
  and and_10 (Load, not_1_out, not_2_out, not_3_out, not_4_out);
  and and_11 (Store, not_1_out, not_2_out, not_3_out, opcode[0]);
  and and_12 (J, not_1_out, opcode[2], not_3_out, opcode[0]);
  and and_13 (Beq, not_1_out, opcode[2], not_3_out, not_4_out);
  and and_14 (RAM_to_reg, not_1_out, not_2_out, not_3_out, not_4_out);
  and and_15 (and_15_out, not_1_out, opcode[2], not_3_out, not_4_out);
  and and_16 (and_16_out, not_1_out, opcode[2], opcode[1], opcode[0]);
  and and_17 (and_17_out, opcode[3], not_2_out, not_3_out, not_4_out);
  or or_1 (write_enable, and_1_out, and_2_out, and_3_out, and_4_out);
  or or_2 (ALU_src, and_8_out, and_9_out);
  or or_3 (Sub, and_15_out, and_16_out, and_17_out);

  assign ALU_op[2] = 1'b0;
endmodule

module imprv_option (
  input  [3:0] Opcode,
  output Reg_Dis,
  output Write_Enable,
  output [2:0] ALU_op,
  output ALU_src,
  output Sub,
  output Store,
  output Load,
  output RAM_to_reg,
  output J,
  output Beq
);

  wire and_2_out, and_3_out, and_4_out, and_5_out, and_8_out, and_9_out, and_10_out, and_11_out, not_1_out,
       not_2_out, not_3_out, not_4_out;

  not not_1 (not_1_out, Opcode[3]);
  not not_2 (not_2_out, Opcode[2]);
  not not_3 (not_3_out, Opcode[1]);
  not not_4 (not_4_out, Opcode[0]);
  and and_1 (Reg_Dis, not_2_out, not_3_out, not_4_out);
  and and_2 (and_2_out, not_2_out, not_3_out, not_4_out);
  and and_3 (and_3_out, not_1_out, Opcode[2], Opcode[1]);
  and and_4 (and_4_out, Opcode[3], not_2_out, not_3_out);
  and and_5 (and_5_out, Opcode[3], not_2_out, not_4_out);
  and and_6 (ALU_op[1], Opcode[3], not_2_out, Opcode[1], not_4_out);
  and and_7 (ALU_op[0], Opcode[3], not_2_out, not_3_out, Opcode[0]);
  and and_8 (and_8_out, not_1_out, not_2_out, not_3_out);
  and and_9 (and_9_out, not_2_out, not_3_out, not_4_out);
  and and_10 (and_10_out, not_1_out, Opcode[2], not_3_out, not_4_out);
  and and_11 (and_11_out, not_1_out, Opcode[2], Opcode[1], Opcode[0]);
  and and_12 (Store, not_1_out, not_2_out, not_3_out, Opcode[0]);
  and and_13 (Load, not_1_out, not_2_out, not_3_out, not_4_out);
  and and_14 (RAM_to_reg, not_1_out, not_2_out, not_3_out, not_4_out);
  and and_15 (J, not_1_out, Opcode[2], not_3_out, Opcode[0]);
  and and_16 (Beq, not_1_out, Opcode[2], not_3_out, not_4_out);
  or or_1 (Write_Enable, and_2_out, and_3_out, and_4_out, and_5_out);
  or or_2 (ALU_src, and_8_out, and_9_out);
  or or_3 (Sub, and_10_out, and_11_out);

  assign ALU_op[2] = 1'b0;
endmodule

module star (
  input  [9:0] in_1,
  output [9:0] Data_1,
  output [9:0] Data_2,
  output [9:0] Result,
  output [3:0] OP,
  output [1:0] rs,
  output [1:0] rt,
  output [1:0] rd_imm_offset
);

  wire and_1_out, clock_1_out, imprv_option_1_alu_src, imprv_option_1_beq, imprv_option_1_j,
       imprv_option_1_load, imprv_option_1_ram_to_reg, imprv_option_1_reg_dis, imprv_option_1_store,
       imprv_option_1_sub, imprv_option_1_write_enable, ten_bitalu_1_zero_signal;
  wire [1:0] multiplexer_3_out;
  wire [2:0] imprv_option_1_alu_op;
  wire [5:0] adder_1_out_2;
  wire [9:0] bit_extender_1_out, multiplexer_1_out, multiplexer_2_out, multiplexer_4_out, multiplexer_5_out,
       ram_1_dout, register_1_q, shifter_1_out;
  wire [9:6] adder_1_out;

  and and_1 (and_1_out, ten_bitalu_1_zero_signal, imprv_option_1_beq);
  Multiplexer #(.width(10)) multiplexer_1 (
    .in0({adder_1_out, adder_1_out_2}), .in1(multiplexer_2_out), .out(multiplexer_1_out), .sel(and_1_out));
  Multiplexer #(.width(10)) multiplexer_2 (
    .in0({adder_1_out, adder_1_out_2}), .in1({adder_1_out, rs, rt, rd_imm_offset}), .out(multiplexer_2_out),
    .sel(imprv_option_1_j));
  ROM #(.addrWidth(10), .dataWidth(10)) rom_1 (.addr(register_1_q), .data({OP, rs, rt, rd_imm_offset}));
  Register #(.width(10)) register_1 (.D(multiplexer_1_out), .Q(register_1_q), .clk(clock_1_out));  // open: en, clr
  Clock clock_1 (.out(clock_1_out));
  imprv_option imprv_option_1 (
    .Write_Enable(imprv_option_1_write_enable), .ALU_op(imprv_option_1_alu_op),
    .ALU_src(imprv_option_1_alu_src), .Sub(imprv_option_1_sub), .Store(imprv_option_1_store),
    .Load(imprv_option_1_load), .RAM_to_reg(imprv_option_1_ram_to_reg), .J(imprv_option_1_j),
    .Beq(imprv_option_1_beq), .Reg_Dis(imprv_option_1_reg_dis), .Opcode(OP));
  Adder #(.width(10)) adder_1 (.a(register_1_q), .b(10'h2), .out({adder_1_out, adder_1_out_2}));  // open: cin, cout
  assign bit_extender_1_out = {{8{rd_imm_offset[1]}}, rd_imm_offset};  // Bit_Extender bit_extender_1
  Multiplexer #(.width(2)) multiplexer_3 (
    .in0(rd_imm_offset), .in1(rt), .out(multiplexer_3_out), .sel(imprv_option_1_reg_dis));
  register_file register_file_1 (
    .out_7(Data_1), .out_8(Data_2), .Write_Enable(imprv_option_1_write_enable), .Clock(clock_1_out),
    .in_1(multiplexer_5_out), .Rd(multiplexer_3_out), .rs(rs), .rt(rt));
  Adder #(.width(10)) adder_2 (.a({adder_1_out, adder_1_out_2}), .b(shifter_1_out));  // open: out, cin, cout
  Shifter #(.width(10)) shifter_1 (.in(bit_extender_1_out), .\dist (in_1[3:0]), .out(shifter_1_out));
  Multiplexer #(.width(10)) multiplexer_4 (
    .in0(Data_2), .in1(bit_extender_1_out), .out(multiplexer_4_out), .sel(imprv_option_1_alu_src));
  ten_bitALU ten_bitalu_1 (
    .out_6(Result), .zero_signal(ten_bitalu_1_zero_signal), .in_5(multiplexer_4_out), .in_1(Data_1),
    .cin(imprv_option_1_sub), .ALU_opcode(imprv_option_1_alu_op), .B_invert(imprv_option_1_sub));  // open: cout, overflow
  RAM #(.addrWidth(10), .asyncread("true"), .dataWidth(10)) ram_1 (
    .addr(Result), .we(imprv_option_1_store), .oe(imprv_option_1_load), .clk(clock_1_out), .din(Data_2),
    .dout(ram_1_dout));
  Multiplexer #(.width(10)) multiplexer_5 (
    .in0(Result), .in1(ram_1_dout), .out(multiplexer_5_out), .sel(imprv_option_1_ram_to_reg));

  // Notes on the sheet:
  //   Clock
  //   Beq s1,s2,2 : 126
  //   J 2:142
  //   contents of rom_1 (hex, n*v repeats v):
  //   26 0 66 0 1ad 0 1ed 0 26d 0 2ad 0 126 0 226 0 226 0 1ad 0 1ed 0 1ed 0 226 0 26d 0 2ad 0 142
  //   Load s1,2 (s2) : 026
  //   Store s1,2(s2) :066
  //   Add s1,s2,s3 : 1ad
  //   Sub s1,s2,s3: 1ed
  //   And s1,s2,s3 :  26d
  //   Or s1,s2,s3  :2ad
  //   Addi s1,s2,2 : 226
  //   6 bit
  //   offset
endmodule

module attempt (
  input  [9:0] in_1,
  output [9:0] Data_1,
  output [9:0] Data_2,
  output [9:0] Result,
  output [3:0] OP,
  output [1:0] rs,
  output [1:0] rt,
  output [1:0] rd_imm_offset
);

  wire and_1_out, attempt_control_1_alu_src, attempt_control_1_beq, attempt_control_1_j,
       attempt_control_1_load, attempt_control_1_ram_to_reg, attempt_control_1_reg_dis,
       attempt_control_1_store, attempt_control_1_sub, attempt_control_1_write_enable, clock_1_out,
       ten_bitalu_1_zero_signal;
  wire [1:0] adder_1_out_2, adder_1_out_3, adder_1_out_4, multiplexer_1_out;
  wire [2:0] attempt_control_1_alu_op;
  wire [3:0] adder_1_out;
  wire [9:0] adder_2_out, bit_extender_1_out, multiplexer_2_out, multiplexer_3_out, multiplexer_4_out,
       multiplexer_5_out, ram_1_dout, register_1_q, shifter_1_out;

  ROM #(.addrWidth(10), .dataWidth(10)) rom_1 (.addr(register_1_q), .data({OP, rs, rt, rd_imm_offset}));
  Register #(.width(10)) register_1 (.D(multiplexer_4_out), .Q(register_1_q), .clk(clock_1_out));  // open: en, clr
  Clock clock_1 (.out(clock_1_out));
  attempt_control attempt_control_1 (
    .Write_Enable(attempt_control_1_write_enable), .ALU_op(attempt_control_1_alu_op),
    .ALU_src(attempt_control_1_alu_src), .Sub(attempt_control_1_sub), .Store(attempt_control_1_store),
    .Load(attempt_control_1_load), .RAM_to_reg(attempt_control_1_ram_to_reg), .J(attempt_control_1_j),
    .Beq(attempt_control_1_beq), .Reg_Dis(attempt_control_1_reg_dis), .Opcode(OP));
  Adder #(.width(10)) adder_1 (
    .a(register_1_q), .b(10'h2), .out({adder_1_out, adder_1_out_4, adder_1_out_3, adder_1_out_2}));  // open: cin, cout
  assign bit_extender_1_out = {{8{rd_imm_offset[1]}}, rd_imm_offset};  // Bit_Extender bit_extender_1
  Multiplexer #(.width(2)) multiplexer_1 (
    .in0(rd_imm_offset), .in1(rt), .out(multiplexer_1_out), .sel(attempt_control_1_reg_dis));
  register_file register_file_1 (
    .out_7(Data_1), .out_8(Data_2), .Write_Enable(attempt_control_1_write_enable), .Clock(clock_1_out),
    .in_1(multiplexer_5_out), .Rd(multiplexer_1_out), .rs(rs), .rt(rt));
  Adder #(.width(10)) adder_2 (
    .a({adder_1_out, adder_1_out_4, adder_1_out_3, adder_1_out_2}), .b(shifter_1_out), .out(adder_2_out));  // open: cin, cout
  Shifter #(.width(10)) shifter_1 (.in(bit_extender_1_out), .\dist (in_1[3:0]), .out(shifter_1_out));
  Multiplexer #(.width(10)) multiplexer_2 (
    .in0({adder_1_out, adder_1_out_4, adder_1_out_3, adder_1_out_2}), .in1(adder_2_out),
    .out(multiplexer_2_out), .sel(and_1_out));
  and and_1 (and_1_out, ten_bitalu_1_zero_signal, attempt_control_1_beq);
  Multiplexer #(.width(10)) multiplexer_3 (
    .in0(Data_2), .in1(bit_extender_1_out), .out(multiplexer_3_out), .sel(attempt_control_1_alu_src));
  Multiplexer #(.width(10)) multiplexer_4 (
    .in0({adder_1_out, adder_1_out_4, adder_1_out_3, adder_1_out_2}), .in1(multiplexer_2_out),
    .out(multiplexer_4_out), .sel(attempt_control_1_j));
  ten_bitALU ten_bitalu_1 (
    .out_6(Result), .zero_signal(ten_bitalu_1_zero_signal), .in_5(multiplexer_3_out), .in_1(Data_1),
    .cin(attempt_control_1_sub), .ALU_opcode(attempt_control_1_alu_op), .B_invert(attempt_control_1_sub));  // open: cout, overflow
  RAM #(.addrWidth(10), .asyncread("true"), .dataWidth(10)) ram_1 (
    .addr(Result), .we(attempt_control_1_store), .oe(attempt_control_1_load), .clk(clock_1_out),
    .din(Data_2), .dout(ram_1_dout));
  Multiplexer #(.width(10)) multiplexer_5 (
    .in0(Result), .in1(ram_1_dout), .out(multiplexer_5_out), .sel(attempt_control_1_ram_to_reg));

  // Notes on the sheet:
  //   Clock
  //   contents of rom_1 (hex, n*v repeats v):
  //   1ad 142 126 0 26 0 226 0 66 0 1ed 0 142 0 126 0 125 0 226 0 226 0 26d 0 1ed 0 26d 0 2ad 0 142
  //   6 bit
  //   offset
endmodule

module attempt_control (
  input  [3:0] Opcode,
  output Reg_Dis,
  output Write_Enable,
  output [2:0] ALU_op,
  output ALU_src,
  output Sub,
  output Store,
  output Load,
  output RAM_to_reg,
  output J,
  output Beq
);

  wire and_2_out, and_3_out, and_4_out, and_5_out, and_9_out, and_10_out, not_1_out, not_2_out, not_3_out,
       not_4_out;

  not not_1 (not_1_out, Opcode[3]);
  not not_2 (not_2_out, Opcode[2]);
  not not_3 (not_3_out, Opcode[1]);
  not not_4 (not_4_out, Opcode[0]);
  and and_1 (Reg_Dis, not_2_out, not_3_out, not_4_out);
  and and_2 (and_2_out, not_2_out, not_3_out, not_4_out);
  and and_3 (and_3_out, not_1_out, Opcode[2], Opcode[1]);
  and and_4 (and_4_out, Opcode[3], not_2_out, not_3_out);
  and and_5 (and_5_out, Opcode[3], not_2_out, not_4_out);
  and and_6 (ALU_op[1], Opcode[3], not_2_out, Opcode[1], not_4_out);
  and and_7 (ALU_op[0], Opcode[3], not_2_out, not_3_out, Opcode[0]);
  and and_8 (ALU_src, not_1_out, not_2_out, not_3_out);
  and and_9 (and_9_out, not_1_out, Opcode[2], not_3_out, not_4_out);
  and and_10 (and_10_out, not_1_out, Opcode[2], Opcode[1], Opcode[0]);
  and and_11 (Store, not_1_out, not_2_out, not_3_out, Opcode[0]);
  and and_12 (Load, not_1_out, not_2_out, not_3_out, not_4_out);
  and and_13 (RAM_to_reg, not_1_out, not_2_out, not_3_out, not_4_out);
  and and_14 (J, not_1_out, Opcode[2], not_3_out, Opcode[0]);
  and and_15 (Beq, not_1_out, Opcode[2], not_3_out, not_4_out);
  or or_1 (Write_Enable, and_2_out, and_3_out, and_4_out, and_5_out);
  or or_2 (Sub, and_9_out, and_10_out);

  assign ALU_op[2] = 1'b0;
endmodule
