// Logisim project Project.circ as structural Verilog: 6 circuits, main circuit main
module main (
);

  One_Bit_ALU one_bit_alu_1 ();  // open: Result, Cout, A, B, Binv, Cin, Opcode
  Register_File register_file_1 ();  // open: Data2, Data1, RD, Enable, Clk, WriteData, RS, RT
  Ten_Bit_ALU_UsingOneBitALU ten_bit_alu_usingonebitalu_1 ();  // open: Result, Cout, Zero, Cin, Op, Binv, A, B
  Control_Unit control_unit_1 ();  // open: Wr_Enable, ALU_Op, ALU_Src, Sub, SW, LW, RAM_To_Reg, Jump, Beq, Reg_Dest, Opcode
endmodule

module One_Bit_ALU (
  input  Binv,
  input  Cin,
  input  A,
  input  B,
  input  [1:0] Opcode,
  output Result,
  output Cout
);

  wire adder_1_out, and_1_out, multiplexer_1_out, not_1_out, or_1_out;

  not not_1 (not_1_out, B);
  Multiplexer #(.enable("true")) multiplexer_1 (
    .in0(B), .in1(not_1_out), .out(multiplexer_1_out), .sel(Binv));  // open: en
  and and_1 (and_1_out, A, multiplexer_1_out);
  or or_1 (or_1_out, A, multiplexer_1_out);
  Adder #(.width(1)) adder_1 (.a(multiplexer_1_out), .b(A), .out(adder_1_out), .cin(Cin), .cout(Cout));
  Multiplexer #(.enable("true"), .select(2)) multiplexer_2 (
    .in0(and_1_out), .in1(or_1_out), .in2(adder_1_out), .out(Result), .sel(Opcode));  // open: in3, en
endmodule

module Ten_Bit_ALU_UsingOneBitALU (
  input  [1:0] Op,
  input  Cin,
  input  Binv,
  input  [9:0] A,
  input  [9:0] B,
  output [9:0] Result,
  output Zero,
  output Cout
);

  wire one_bit_alu_1_cout, one_bit_alu_2_cout, one_bit_alu_3_cout, one_bit_alu_4_cout, one_bit_alu_5_cout,
       one_bit_alu_6_cout, one_bit_alu_7_cout, one_bit_alu_8_cout, one_bit_alu_9_cout;

  One_Bit_ALU one_bit_alu_1 (
    .Result(Result[0]), .Cout(one_bit_alu_1_cout), .A(A[0]), .B(B[0]), .Binv(Binv), .Cin(Cin), .Opcode(Op));
  One_Bit_ALU one_bit_alu_2 (
    .Result(Result[1]), .Cout(one_bit_alu_2_cout), .A(A[1]), .B(B[1]), .Binv(Binv), .Cin(one_bit_alu_1_cout),
    .Opcode(Op));
  One_Bit_ALU one_bit_alu_3 (
    .Result(Result[2]), .Cout(one_bit_alu_3_cout), .A(A[2]), .B(B[2]), .Binv(Binv), .Cin(one_bit_alu_2_cout),
    .Opcode(Op));
  One_Bit_ALU one_bit_alu_4 (
    .Result(Result[3]), .Cout(one_bit_alu_4_cout), .A(A[3]), .B(B[3]), .Binv(Binv), .Cin(one_bit_alu_3_cout),
    .Opcode(Op));
  One_Bit_ALU one_bit_alu_5 (
    .Result(Result[4]), .Cout(one_bit_alu_5_cout), .A(A[4]), .B(B[4]), .Binv(Binv), .Cin(one_bit_alu_4_cout),
    .Opcode(Op));
  One_Bit_ALU one_bit_alu_6 (
    .Result(Result[5]), .Cout(one_bit_alu_6_cout), .A(A[5]), .B(B[5]), .Binv(Binv), .Cin(one_bit_alu_5_cout),
    .Opcode(Op));
  One_Bit_ALU one_bit_alu_7 (
    .Result(Result[6]), .Cout(one_bit_alu_7_cout), .A(A[6]), .B(B[6]), .Binv(Binv), .Cin(one_bit_alu_6_cout),
    .Opcode(Op));
  One_Bit_ALU one_bit_alu_8 (
    .Result(Result[7]), .Cout(one_bit_alu_8_cout), .A(A[7]), .B(B[7]), .Binv(Binv), .Cin(one_bit_alu_7_cout),
    .Opcode(Op));
  One_Bit_ALU one_bit_alu_9 (
    .Result(Result[8]), .Cout(one_bit_alu_9_cout), .A(A[8]), .B(B[8]), .Binv(Binv), .Cin(one_bit_alu_8_cout),
    .Opcode(Op));
  One_Bit_ALU one_bit_alu_10 (
    .Result(Result[9]), .Cout(Cout), .A(A[9]), .B(B[9]), .Binv(Binv), .Cin(one_bit_alu_9_cout), .Opcode(Op));
  nor nor_1 (Zero, Result[0], Result[1], Result[2], Result[3], Result[4], Result[5], Result[6], Result[7], Result[8], Result[9]);
endmodule

module Register_File (
  input  [9:0] WriteData,
  input  [1:0] RS,
  input  [1:0] RT,
  input  [1:0] RD,
  input  Enable,
  input  Clk,
  output [9:0] Data1,
  output [9:0] Data2
);

  wire and_1_out, and_2_out, and_3_out, and_4_out, decoder_1_out0, decoder_1_out1, decoder_1_out2,
       decoder_1_out3;
  wire [9:0] R0_q, R1_q, R2_q, R3_q;

  Decoder #(.enable("false"), .select(2)) decoder_1 (
    .out0(decoder_1_out0), .out1(decoder_1_out1), .out2(decoder_1_out2), .out3(decoder_1_out3), .sel(RD));
  and and_1 (and_1_out, decoder_1_out0, Enable);
  and and_2 (and_2_out, decoder_1_out1, Enable);
  and and_3 (and_3_out, decoder_1_out2, Enable);
  and and_4 (and_4_out, decoder_1_out3, Enable);
  Register #(.width(10)) R0 (.D(WriteData), .en(and_1_out), .Q(R0_q), .clk(Clk));  // open: clr
  Register #(.width(10)) R1 (.D(WriteData), .en(and_2_out), .Q(R1_q), .clk(Clk));  // open: clr
  Register #(.width(10)) R2 (.D(WriteData), .en(and_3_out), .Q(R2_q), .clk(Clk));  // open: clr
  Register #(.width(10)) R3 (.D(WriteData), .en(and_4_out), .Q(R3_q), .clk(Clk));  // open: clr
  Multiplexer #(.enable("true"), .select(2), .width(10)) multiplexer_1 (
    .in0(R0_q), .in1(R1_q), .in2(R2_q), .in3(R3_q), .out(Data1), .sel(RS));  // open: en
  Multiplexer #(.enable("true"), .select(2), .width(10)) multiplexer_2 (
    .in0(R0_q), .in1(R1_q), .in2(R2_q), .in3(R3_q), .out(Data2), .sel(RT));  // open: en
endmodule

module Control_Unit (
  input  [3:0] Opcode,
  output Reg_Dest,
  output Wr_Enable,
  output [1:0] ALU_Op,
  output ALU_Src,
  output Sub,
  output SW,
  output LW,
  output RAM_To_Reg,
  output Jump,
  output Beq
);

  wire and_1_out, and_2_out, and_3_out, and_4_out, and_5_out, and_6_out, and_7_out, and_8_out, and_10_out,
       and_11_out, and_12_out, and_13_out, and_14_out, and_19_out, and_20_out, not_1_out, not_2_out,
       not_3_out, not_4_out;

  not not_1 (not_1_out, Opcode[3]);
  not not_2 (not_2_out, Opcode[2]);
  not not_3 (not_3_out, Opcode[1]);
  not not_4 (not_4_out, Opcode[0]);
  and and_1 (and_1_out, not_1_out, Opcode[1], not_4_out);
  and and_2 (and_2_out, not_1_out, Opcode[2], not_3_out, Opcode[0]);
  and and_3 (and_3_out, Opcode[3], not_2_out, not_3_out, not_4_out);
  and and_4 (and_4_out, not_1_out, not_3_out, not_4_out);
  and and_5 (and_5_out, not_1_out, not_2_out, Opcode[0]);
  and and_6 (and_6_out, not_2_out, not_3_out);
  and and_7 (and_7_out, not_1_out, Opcode[1], not_4_out);
  and and_8 (and_8_out, not_1_out, Opcode[2], Opcode[0]);
  and and_9 (ALU_Op[0], not_1_out, Opcode[2], not_3_out, not_4_out);
  and and_10 (and_10_out, not_1_out, Opcode[1], not_4_out);
  and and_11 (and_11_out, not_1_out, Opcode[2], not_3_out, Opcode[0]);
  and and_12 (and_12_out, Opcode[3], not_2_out, not_3_out);
  and and_13 (and_13_out, not_1_out, not_3_out, Opcode[0]);
  and and_14 (and_14_out, not_1_out, Opcode[2], Opcode[1], not_4_out);
  and and_15 (SW, Opcode[3], not_2_out, not_3_out, Opcode[0]);
  and and_16 (LW, Opcode[3], not_2_out, not_3_out, not_4_out);
  and and_17 (RAM_To_Reg, Opcode[3], not_2_out, not_3_out, not_4_out);
  and and_18 (Jump, not_1_out, Opcode[2], Opcode[1], Opcode[0]);
  and and_19 (and_19_out, not_1_out, Opcode[2], not_3_out, Opcode[0]);
  and and_20 (and_20_out, not_1_out, Opcode[2], Opcode[1], not_4_out);
  or or_1 (Reg_Dest, and_1_out, and_2_out, and_3_out);
  or or_2 (Wr_Enable, and_4_out, and_5_out);
  or or_3 (ALU_Op[1], and_6_out, and_7_out, and_8_out);
  or or_4 (ALU_Src, and_10_out, and_11_out, and_12_out);
  or or_5 (Sub, and_13_out, and_14_out);
  or or_6 (Beq, and_19_out, and_20_out);
endmodule

module Full_Single_Cycle_Datapath (
  input  [9:0] in_1,
  output [9:0] out_2,
  output [9:0] out_3,
  output [3:0] Opcode,
  output [1:0] RS,
  output [1:0] RT,
  output [1:0] RD__Imm__Offset,
  output [9:0] Result,
  output [9:0] Data_For_Store,
  output out_10
);

  wire and_1_out, clock_1_out, control_unit_1_alu_src, control_unit_1_beq, control_unit_1_jump,
       control_unit_1_lw, control_unit_1_ram_to_reg, control_unit_1_reg_dest, control_unit_1_sub,
       control_unit_1_sw, control_unit_1_wr_enable, ten_bit_alu_usingonebitalu_1_zero;
  wire [1:0] adder_1_out_2, adder_1_out_3, adder_1_out_4, control_unit_1_alu_op, multiplexer_1_out;
  wire [3:0] adder_1_out;
  wire [9:0] adder_2_out, bit_extender_1_out, multiplexer_3_out, multiplexer_4_out, ram_1_dout, register_1_q,
       shifter_1_out, ten_bit_alu_usingonebitalu_1_result;

  Register #(.width(10)) register_1 (.D(multiplexer_4_out), .Q(register_1_q), .clk(clock_1_out));  // open: en, clr
  Adder #(.width(10)) adder_1 (
    .a(register_1_q), .b(10'h1), .out({adder_1_out, adder_1_out_4, adder_1_out_3, adder_1_out_2}));  // open: cin, cout
  ROM #(.addrWidth(10), .dataWidth(10)) rom_1 (.addr(register_1_q), .data({Opcode, RS, RT, RD__Imm__Offset}));
  Control_Unit control_unit_1 (
    .Wr_Enable(control_unit_1_wr_enable), .ALU_Op(control_unit_1_alu_op), .ALU_Src(control_unit_1_alu_src),
    .Sub(control_unit_1_sub), .SW(control_unit_1_sw), .LW(control_unit_1_lw),
    .RAM_To_Reg(control_unit_1_ram_to_reg), .Jump(control_unit_1_jump), .Beq(control_unit_1_beq),
    .Reg_Dest(control_unit_1_reg_dest), .Opcode(Opcode));
  Clock clock_1 (.out(clock_1_out));
  Multiplexer #(.width(2)) multiplexer_1 (
    .in0(RD__Imm__Offset), .in1(RT), .out(multiplexer_1_out), .sel(control_unit_1_reg_dest));
  assign bit_extender_1_out = {{8{RD__Imm__Offset[1]}}, RD__Imm__Offset};  // Bit_Extender bit_extender_1
  Register_File register_file_1 (
    .Data2(Data_For_Store), .Data1(out_2), .RD(multiplexer_1_out), .Enable(control_unit_1_wr_enable),
    .Clk(clock_1_out), .WriteData(Result), .RS(RS), .RT(RD__Imm__Offset));
  Shifter #(.width(10)) shifter_1 (.in(bit_extender_1_out), .\dist (in_1[3:0]), .out(shifter_1_out));
  Multiplexer #(.width(10)) multiplexer_2 (
    .in0(Data_For_Store), .in1(bit_extender_1_out), .out(out_3), .sel(control_unit_1_alu_src));
  Adder #(.width(10)) adder_2 (
    .a({adder_1_out, adder_1_out_4, adder_1_out_3, adder_1_out_2}), .b(shifter_1_out), .out(adder_2_out));  // open: cin, cout
  Ten_Bit_ALU_UsingOneBitALU ten_bit_alu_usingonebitalu_1 (
    .Result(ten_bit_alu_usingonebitalu_1_result), .Cout(out_10), .Zero(ten_bit_alu_usingonebitalu_1_zero),
    .Cin(control_unit_1_sub), .Op(control_unit_1_alu_op), .Binv(control_unit_1_sub), .A(out_2), .B(out_3));
  Multiplexer #(.width(10)) multiplexer_3 (
    .in0({adder_1_out, adder_1_out_4, adder_1_out_3, adder_1_out_2}), .in1(adder_2_out),
    .out(multiplexer_3_out), .sel(and_1_out));
  and and_1 (and_1_out, ten_bit_alu_usingonebitalu_1_zero, control_unit_1_beq);
  Multiplexer #(.width(10)) multiplexer_4 (
    .in0(multiplexer_3_out), .in1({adder_1_out, RS, RT, RD__Imm__Offset}), .out(multiplexer_4_out),
    .sel(control_unit_1_jump));
  RAM #(.addrWidth(10), .asyncread("true"), .dataWidth(10)) ram_1 (
    .addr(ten_bit_alu_usingonebitalu_1_result), .we(control_unit_1_sw), .oe(control_unit_1_lw),
    .clk(clock_1_out), .din(Data_For_Store), .dout(ram_1_dout));
  Multiplexer #(.width(10)) multiplexer_5 (
    .in0(ten_bit_alu_usingonebitalu_1_result), .in1(ram_1_dout), .out(Result), .sel(control_unit_1_ram_to_reg));

  // Notes on the sheet:
  //   Clock
  //   6 bit
  //   offset
  //   Data 1
  //   Data 2
endmodule
